# Fritzing sketch Seite_099_Schalter (saved by Fritzing 0.9.1b)
breadboards: 1

parts:
  Raspberry_Pi_B_rev1 = Raspberry Pi B rev1
  R1 = Resistor [tolerance=±5% resistance=10k package=THT]
  S1 = Pushbutton [package="[THT]"]

nets:
  N1: Raspberry_Pi_B_rev1.3V3, S1.Pin_3, S1.Pin_4
  N2: Raspberry_Pi_B_rev1.GPIO_23, R1.Pin_1, S1.Pin_1, S1.Pin_2
  N3: Raspberry_Pi_B_rev1.GND, R1.Pin_0
