# Fritzing sketch Seite_108_Servo (saved by Fritzing 0.9.1b)

parts:
  Raspberry_Pi_B_rev1 = Raspberry Pi B rev1
  J1 = Basic Servo

nets:
  3V3: Raspberry_Pi_B_rev1.3V3, J1.vcc
  N1: Raspberry_Pi_B_rev1.GPIO_23, J1.pulse
  GND: Raspberry_Pi_B_rev1.GND, J1.gnd
