# Fritzing sketch Seite_125_Pro_Mini (saved by Fritzing 0.9.1b)

parts:
  Bauteil1 = Arduino Pro Mini v13 - different Raster
  Raspberry_Pi1 = Raspberry Pi B rev2

nets:
  N1: Bauteil1.DTR, Raspberry_Pi1.GPIO_18
  N2: Bauteil1.D0/TX, Raspberry_Pi1.GPIO_15
  N3: Bauteil1.D1/RX, Raspberry_Pi1.GPIO_14
  VCC: Bauteil1.VCC, Raspberry_Pi1.3V3
  GND: Bauteil1.GND, Raspberry_Pi1.GND

custom parts:
  Arduino Pro Mini v13 - different Raster: It's blue! It's thin! It's the Arduino Pro Mini! SparkFun's minimal design approach to Arduino. This is a 5V Arduino running the 16MHz bootloader. Arduino Pro Mini does not come with connectors populated so that you can solder in any connector or wire with any orientation you need. We recommend first time Arduino users start with the Uno R3. It's a great board that will get you up and running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
